// Logisim project inst mem3.circ as structural Verilog: 12 circuits, main circuit main
module main (
  input  RESET
);

  wire alu_1_neq, BRANCH_out, clock_1_out, control_1_alu_src, control_1_bne, control_1_jump,
       control_1_mem_write, control_1_reg_dest, control_1_reg_load, control_1_reg_src, not_1_out;
  wire [2:0] control_1_alu_op;
  wire [3:0] multiplexer_1_out;
  wire [15:0] adder_1_out, adder_2_out, alu_1_r, bit_extender_1_out, bit_extender_2_out, multiplexer_2_out,
       multiplexer_3_out, multiplexer_4_out, multiplexer_5_out, ram_1_data, register_1_q,
       register_file_1_b_data, register_file_1_c_data, rom_1_data;

  Adder #(.width(16)) adder_1 (.a(16'h1), .b(multiplexer_4_out), .out(adder_1_out));  // open: cin, cout
  Register #(.width(16)) register_1 (.D(adder_1_out), .Q(register_1_q), .clk(clock_1_out), .clr(RESET));  // open: en
  ROM #(.addrWidth(16), .dataWidth(16)) rom_1 (.addr(register_1_q), .data(rom_1_data));  // open: sel
  Adder #(.width(16)) adder_2 (.a(register_1_q), .b(bit_extender_1_out), .out(adder_2_out));  // open: cin, cout
  control control_1 (
    .op(rom_1_data[15:12]), .alu_op(control_1_alu_op), .alu_src(control_1_alu_src),
    .reg_src(control_1_reg_src), .reg_dest(control_1_reg_dest), .mem_write(control_1_mem_write),
    .reg_load(control_1_reg_load), .bne(control_1_bne), .jump(control_1_jump));
  Multiplexer #(.width(4), .enable("false")) multiplexer_1 (
    .in0(rom_1_data[3:0]), .in1(rom_1_data[11:8]), .out(multiplexer_1_out), .sel(control_1_reg_dest));
  assign bit_extender_1_out = {{12{rom_1_data[3]}}, rom_1_data[3:0]};  // Bit_Extender bit_extender_1
  Clock clock_1 (.out(clock_1_out));
  register_file register_file_1 (
    .b_addr(rom_1_data[7:4]), .c_addr(multiplexer_1_out), .a_data(multiplexer_5_out), .CLK(clock_1_out),
    .CLEAR(not_1_out), .a_addr(rom_1_data[11:8]), .load(control_1_reg_load), .b_data(register_file_1_b_data),
    .c_data(register_file_1_c_data));
  not not_1 (not_1_out, RESET);
  Multiplexer #(.width(16), .enable("false")) multiplexer_2 (
    .in0(register_1_q), .in1(adder_2_out), .out(multiplexer_2_out), .sel(BRANCH_out));
  and BRANCH (BRANCH_out, control_1_bne, alu_1_neq);
  Multiplexer #(.width(16), .enable("false")) multiplexer_3 (
    .in0(register_file_1_c_data), .in1(bit_extender_1_out), .out(multiplexer_3_out), .sel(control_1_alu_src));
  alu alu_1 (.S(control_1_alu_op), .A(register_file_1_b_data), .B(multiplexer_3_out), .R(alu_1_r), .neq(alu_1_neq));
  assign bit_extender_2_out = {{4{1'b0}}, {rom_1_data[3:0], rom_1_data[7:4], rom_1_data[11:8]}};  // Bit_Extender bit_extender_2
  RAM #(.addrWidth(16), .dataWidth(16), .bus("separate")) ram_1 (
    .addr(alu_1_r), .din(register_file_1_c_data), .data(ram_1_data), .str(control_1_mem_write),
    .clk(clock_1_out), .clr(RESET));  // open: sel, ld
  Multiplexer #(.width(16), .enable("false")) multiplexer_4 (
    .in0(multiplexer_2_out), .in1(bit_extender_2_out), .out(multiplexer_4_out), .sel(control_1_jump));
  Multiplexer #(.width(16), .enable("false")) multiplexer_5 (
    .in0(ram_1_data), .in1(alu_1_r), .out(multiplexer_5_out), .sel(control_1_reg_src));

  // Notes on the sheet:
  //   contents of rom_1 (hex, n*v repeats v):
  //   211 4321 1431 5541 2655 3755 7832 c301 8901 9339
endmodule

module register_file (
  input  [3:0] b_addr,
  input  [3:0] c_addr,
  input  [15:0] a_data,
  input  CLK,
  input  CLEAR,
  input  [3:0] a_addr,
  input  load,
  output [15:0] b_data,
  output [15:0] c_data
);

  wire demultiplexer_1_out2, demultiplexer_1_out3, demultiplexer_1_out4, demultiplexer_1_out5,
       demultiplexer_1_out6, demultiplexer_1_out7, demultiplexer_1_out8, demultiplexer_1_out9,
       demultiplexer_1_out10, demultiplexer_1_out11, demultiplexer_1_out12, demultiplexer_1_out13,
       demultiplexer_1_out14, demultiplexer_1_out15, not_1_out;
  wire [15:0] Q02, Q03, Q04, Q05, Q06, Q07, Q08, Q09, Q10, Q11, Q12, Q13, Q14, Q15;

  not not_1 (not_1_out, CLEAR);
  Demultiplexer #(.select(4), .enable("false")) demultiplexer_1 (
    .out2(demultiplexer_1_out2), .out3(demultiplexer_1_out3), .out4(demultiplexer_1_out4),
    .out5(demultiplexer_1_out5), .out6(demultiplexer_1_out6), .out7(demultiplexer_1_out7),
    .out8(demultiplexer_1_out8), .out9(demultiplexer_1_out9), .out10(demultiplexer_1_out10),
    .out11(demultiplexer_1_out11), .out12(demultiplexer_1_out12), .out13(demultiplexer_1_out13),
    .out14(demultiplexer_1_out14), .out15(demultiplexer_1_out15), .in(load), .sel(a_addr));  // open: out0, out1
  Register #(.width(16)) register_1 (.D(a_data), .en(demultiplexer_1_out2), .Q(Q02), .clk(CLK), .clr(not_1_out));
  Register #(.width(16)) register_2 (.D(a_data), .en(demultiplexer_1_out3), .Q(Q03), .clk(CLK), .clr(not_1_out));
  Multiplexer #(.select(4), .width(16), .enable("false")) multiplexer_1 (
    .in0({16{1'b0}}), .in1(16'h1), .in2(Q02), .in3(Q03), .in4(Q04), .in5(Q05), .in6(Q06), .in7(Q07),
    .in8(Q08), .in9(Q09), .in10(Q10), .in11(Q11), .in12(Q12), .in13(Q13), .in14(Q14), .in15(Q15),
    .out(c_data), .sel(c_addr));
  Register #(.width(16)) register_3 (.D(a_data), .en(demultiplexer_1_out4), .Q(Q04), .clk(CLK), .clr(not_1_out));
  Register #(.width(16)) register_4 (.D(a_data), .en(demultiplexer_1_out5), .Q(Q05), .clk(CLK), .clr(not_1_out));
  Register #(.width(16)) register_5 (.D(a_data), .en(demultiplexer_1_out6), .Q(Q06), .clk(CLK), .clr(not_1_out));
  Register #(.width(16)) register_6 (.D(a_data), .en(demultiplexer_1_out7), .Q(Q07), .clk(CLK), .clr(not_1_out));
  Register #(.width(16)) register_7 (.D(a_data), .en(demultiplexer_1_out8), .Q(Q08), .clk(CLK), .clr(not_1_out));
  Register #(.width(16)) register_8 (.D(a_data), .en(demultiplexer_1_out9), .Q(Q09), .clk(CLK), .clr(not_1_out));
  Register #(.width(16)) register_9 (.D(a_data), .en(demultiplexer_1_out10), .Q(Q10), .clk(CLK), .clr(not_1_out));
  Register #(.width(16)) register_10 (.D(a_data), .en(demultiplexer_1_out11), .Q(Q11), .clk(CLK), .clr(not_1_out));
  Multiplexer #(.select(4), .width(16), .enable("false")) multiplexer_2 (
    .in0({16{1'b0}}), .in1(16'h1), .in2(Q02), .in3(Q03), .in4(Q04), .in5(Q05), .in6(Q06), .in7(Q07),
    .in8(Q08), .in9(Q09), .in10(Q10), .in11(Q11), .in12(Q12), .in13(Q13), .in14(Q14), .in15(Q15),
    .out(b_data), .sel(b_addr));
  Register #(.width(16)) register_11 (.D(a_data), .en(demultiplexer_1_out12), .Q(Q12), .clk(CLK), .clr(not_1_out));
  Register #(.width(16)) register_12 (.D(a_data), .en(demultiplexer_1_out13), .Q(Q13), .clk(CLK), .clr(not_1_out));
  Register #(.width(16)) register_13 (.D(a_data), .en(demultiplexer_1_out14), .Q(Q14), .clk(CLK), .clr(not_1_out));
  Register #(.width(16)) register_14 (.D(a_data), .en(demultiplexer_1_out15), .Q(Q15), .clk(CLK), .clr(not_1_out));
endmodule

module alu (
  input  [2:0] S,
  input  [15:0] A,
  input  [15:0] B,
  output [15:0] R,
  output neq
);

  wire comparator_1_eq, comparator_1_lt;
  wire [15:0] adder_1_out, and_1_out, bit_extender_1_out, or_1_out, subtractor_1_out;

  Adder #(.width(16)) adder_1 (.a(A), .b(B), .out(adder_1_out));  // open: cin, cout
  Subtractor #(.width(16)) subtractor_1 (.a(A), .b(B), .out(subtractor_1_out));  // open: bin, bout
  assign and_1_out = A & B;  // AND_Gate and_1, 16 bits wide
  assign or_1_out = A | B;  // OR_Gate or_1, 16 bits wide
  Comparator #(.width(16)) comparator_1 (.a(A), .b(B), .eq(comparator_1_eq), .lt(comparator_1_lt));  // open: gt
  assign bit_extender_1_out = {{15{1'b0}}, comparator_1_lt};  // Bit_Extender bit_extender_1
  Multiplexer #(.select(3), .width(16), .enable("false")) multiplexer_1 (
    .in0(adder_1_out), .in1(subtractor_1_out), .in2(and_1_out), .in3(or_1_out), .in4(bit_extender_1_out),
    .out(R), .sel(S));  // open: in5, in6, in7
  not not_1 (neq, comparator_1_eq);
endmodule

module control (
  input  [3:0] op,
  output [2:0] alu_op,
  output alu_src,
  output reg_src,
  output reg_dest,
  output mem_write,
  output reg_load,
  output bne,
  output jump
);

  control_alu_op control_alu_op_1 (.opcode(op), .alu_op(alu_op));
  control_alu_s control_alu_s_1 (.opcode(op), .alu_src(alu_src));
  control_reg_src control_reg_src_1 (.opcode(op), .reg_src(reg_src));
  control_reg_dest control_reg_dest_1 (.opcode(op), .out_2(reg_dest));
  control_mem_write control_mem_write_1 (.opcode(op), .mem_write(mem_write));
  control_reg_load control_reg_load_1 (.opcode(op), .reg_load(reg_load));
  control_bne control_bne_1 (.in_1(op), .out_2(bne));
  control_jump control_jump_1 (.in_1(op), .out_2(jump));
endmodule

module control_alu_op (
  input  [3:0] opcode,
  output [2:0] alu_op
);

  Multiplexer #(.select(4), .width(3), .enable("false")) multiplexer_1 (
    .in0(3'b000), .in1(3'b001), .in2(3'b010), .in3(3'b011), .in4(3'b000), .in5(3'b001), .in7(3'b100),
    .in8(3'b000), .in12(3'b000), .out(alu_op), .sel(opcode));  // open: in6, in9, in10, in11, in13, in14, in15
endmodule

module control_alu_s (
  input  [3:0] opcode,
  output alu_src
);

  Multiplexer #(.select(4), .disabled(0), .enable("false")) multiplexer_1 (
    .in0(1'b0), .in1(1'b0), .in2(1'b0), .in3(1'b0), .in4(1'b1), .in5(1'b1), .in7(1'b0), .in8(1'b1),
    .in9(1'b0), .in12(1'b1), .out(alu_src), .sel(opcode));  // open: in6, in10, in11, in13, in14, in15
endmodule

module control_reg_src (
  input  [3:0] opcode,
  output reg_src
);

  wire comparator_1_eq;

  Comparator #(.width(4)) comparator_1 (.a(opcode), .b(4'b1000), .eq(comparator_1_eq));  // open: gt, lt
  not not_1 (reg_src, comparator_1_eq);
endmodule

module control_reg_dest (
  input  [3:0] opcode,
  output out_2
);

  wire comparator_1_eq, comparator_2_eq;

  Comparator #(.width(4)) comparator_1 (.a(opcode), .b(4'b1100), .eq(comparator_1_eq));  // open: gt, lt
  Comparator #(.width(4)) comparator_2 (.a(opcode), .b(4'b1001), .eq(comparator_2_eq));  // open: gt, lt
  or or_1 (out_2, comparator_1_eq, comparator_2_eq);
endmodule

module control_mem_write (
  input  [3:0] opcode,
  output mem_write
);

  Comparator #(.width(4)) comparator_1 (.a(opcode), .b(4'b1100), .eq(mem_write));  // open: gt, lt
endmodule

module control_reg_load (
  input  [3:0] opcode,
  output reg_load
);

  wire comparator_1_eq;

  Comparator #(.width(4)) comparator_1 (.a(opcode), .b(4'b1100), .eq(comparator_1_eq));  // open: gt, lt
  not not_1 (reg_load, comparator_1_eq);
endmodule

module control_bne (
  input  [3:0] in_1,
  output out_2
);

  Comparator #(.width(4)) comparator_1 (.a(in_1), .b(4'b1001), .eq(out_2));  // open: gt, lt
endmodule

module control_jump (
  input  [3:0] in_1,
  output out_2
);

  Comparator #(.width(4)) comparator_1 (.a(in_1), .b(4'b1011), .eq(out_2));  // open: gt, lt
endmodule
